// Digital circuit 4bit-MULT.dig as structural Verilog
module _4bit_MULT (
  input  [3:0] B,
  input  [3:0] A,
  output [7:0] P,
  output Cout
);

  wire _8bit_ad_1_cout, _8bit_ad_2_cout;
  wire [3:0] A1, A2, A3, A4;
  wire [7:0] _8bit_ad_1_s, _8bit_ad_2_s, _8bit_lshift_1_as, _8bit_lshift_2_as, _8bit_lshift_3_as,
       _8bit_lshift_4_as, _8bit_lshift_5_as, _8bit_lshift_6_as;

  _8bit_LShift _8bit_lshift_1 (.A({4'b0000, A4}), .As(_8bit_lshift_1_as));
  _8bit_LShift _8bit_lshift_2 (.A({4'b0000, A3}), .As(_8bit_lshift_2_as));
  _8bit_LShift _8bit_lshift_3 (.A({4'b0000, A2}), .As(_8bit_lshift_3_as));
  _8bit_LShift _8bit_lshift_4 (.A(_8bit_lshift_1_as), .As(_8bit_lshift_4_as));
  _8bit_LShift _8bit_lshift_5 (.A(_8bit_lshift_2_as), .As(_8bit_lshift_5_as));
  _8bit_LShift _8bit_lshift_6 (.A(_8bit_lshift_4_as), .As(_8bit_lshift_6_as));
  and and_1 (A1[0], A[0], B[0]);
  _8bit_AD _8bit_ad_1 (.A(_8bit_lshift_3_as), .B({4'b0000, A1}), .Cin(1'b0), .S(_8bit_ad_1_s), .Cout(_8bit_ad_1_cout));
  and and_2 (A1[1], A[1], B[0]);
  _8bit_AD _8bit_ad_2 (
    .A(_8bit_lshift_5_as), .B(_8bit_ad_1_s), .Cin(_8bit_ad_1_cout), .S(_8bit_ad_2_s), .Cout(_8bit_ad_2_cout));
  and and_3 (A1[2], A[2], B[0]);
  _8bit_AD _8bit_ad_3 (.A(_8bit_lshift_6_as), .B(_8bit_ad_2_s), .Cin(_8bit_ad_2_cout), .S(P), .Cout(Cout));
  and and_4 (A1[3], A[3], B[0]);
  and and_5 (A2[0], A[0], B[1]);
  and and_6 (A2[1], A[1], B[1]);
  and and_7 (A2[2], A[2], B[1]);
  and and_8 (A2[3], A[3], B[1]);
  and and_9 (A3[0], A[0], B[2]);
  and and_10 (A3[1], A[1], B[2]);
  and and_11 (A3[2], A[2], B[2]);
  and and_12 (A3[3], A[3], B[2]);
  and and_13 (A4[0], A[0], B[3]);
  and and_14 (A4[1], A[1], B[3]);
  and and_15 (A4[2], A[2], B[3]);
  and and_16 (A4[3], A[3], B[3]);

  // Other names for the same wires on the sheet: B1 = B[0]; B2 = B[1]; B3 = B[2]; B4 = B[3]
endmodule
