// Digital circuit 8bit-AD.dig as structural Verilog
module _8bit_AD (
  input  [7:0] A,
  input  [7:0] B,
  input  Cin,
  output [7:0] S,
  output Cout
);

  wire ad_1_cout, ad_2_cout, ad_3_cout, ad_4_cout, ad_5_cout, ad_6_cout, ad_7_cout, ad_8_cout;

  AD ad_1 (.Cin(Cin), .A(A[0]), .B(B[0]), .Sum(S[0]), .Cout(ad_1_cout));
  AD ad_2 (.Cin(ad_1_cout), .A(A[1]), .B(B[1]), .Sum(S[1]), .Cout(ad_2_cout));
  AD ad_3 (.Cin(ad_2_cout), .A(A[2]), .B(B[2]), .Sum(S[2]), .Cout(ad_3_cout));
  AD ad_4 (.Cin(ad_3_cout), .A(A[3]), .B(B[3]), .Sum(S[3]), .Cout(ad_4_cout));
  AD ad_5 (.Cin(ad_4_cout), .A(A[4]), .B(B[4]), .Sum(S[4]), .Cout(ad_5_cout));
  AD ad_6 (.Cin(ad_5_cout), .A(A[5]), .B(B[5]), .Sum(S[5]), .Cout(ad_6_cout));
  AD ad_7 (.Cin(ad_6_cout), .A(A[6]), .B(B[6]), .Sum(S[6]), .Cout(ad_7_cout));
  AD ad_8 (.Cin(ad_7_cout), .A(A[7]), .B(B[7]), .Sum(S[7]), .Cout(ad_8_cout));
  xor xor_1 (Cout, ad_8_cout, ad_7_cout);

  // Notes on the sheet:
  //   S: Soma dos dois números.
endmodule
