// Digital circuit 8bit-COMP.dig as structural Verilog
module _8bit_COMP (
  input  [7:0] A,
  input  [7:0] B,
  output gt,
  output lt,
  output eq
);

  wire comp_1_eq, comp_1_gt, comp_1_lt, comp_2_eq, comp_2_gt, comp_2_lt, comp_3_eq, comp_3_gt, comp_3_lt,
       comp_4_eq, comp_4_gt, comp_4_lt, comp_5_eq, comp_5_gt, comp_5_lt, comp_6_eq, comp_6_gt, comp_6_lt,
       comp_7_eq, comp_7_gt, comp_7_lt, comp_8_gt, comp_8_lt;

  COMP comp_1 (.gt(comp_1_gt), .lt(comp_1_lt), .eq(comp_1_eq), ._1_eq(1'b1), .A(A[7]), .B(B[7]));
  COMP comp_2 (.gt(comp_2_gt), .lt(comp_2_lt), .eq(comp_2_eq), ._1_eq(comp_1_eq), .A(A[6]), .B(B[6]));
  COMP comp_3 (.gt(comp_3_gt), .lt(comp_3_lt), .eq(comp_3_eq), ._1_eq(comp_2_eq), .A(A[5]), .B(B[5]));
  COMP comp_4 (.gt(comp_4_gt), .lt(comp_4_lt), .eq(comp_4_eq), ._1_eq(comp_3_eq), .A(A[4]), .B(B[4]));
  COMP comp_5 (.gt(comp_5_gt), .lt(comp_5_lt), .eq(comp_5_eq), ._1_eq(comp_4_eq), .A(A[3]), .B(B[3]));
  COMP comp_6 (.gt(comp_6_gt), .lt(comp_6_lt), .eq(comp_6_eq), ._1_eq(comp_5_eq), .A(A[2]), .B(B[2]));
  COMP comp_7 (.gt(comp_7_gt), .lt(comp_7_lt), .eq(comp_7_eq), ._1_eq(comp_6_eq), .A(A[1]), .B(B[1]));
  COMP comp_8 (.gt(comp_8_gt), .lt(comp_8_lt), .eq(eq), ._1_eq(comp_7_eq), .A(A[0]), .B(B[0]));
  xor xor_1 (gt, comp_8_gt, comp_2_gt, comp_3_gt, comp_4_gt, comp_5_gt, comp_6_gt, comp_7_gt, comp_1_lt);
  xor xor_2 (lt, comp_1_gt, comp_7_lt, comp_6_lt, comp_5_lt, comp_4_lt, comp_3_lt, comp_2_lt, comp_8_lt);

  // Notes on the sheet:
  //   A: Entrada de 8 bits para o primeiro valor
  //   B: Entrada de 8 bits para o segundo valor
  //   gt: Siginfica que A > B, ou seja, primeiro valor é maior que o segundo valor.
  //   lt: Siginfica que A < B, ou seja, primeiro valor é menor que o segundo valor.
  //   eq: Siginfica que A = B, ou seja, primeiro valor é igual ao segundo valor.
endmodule
