// Digital circuit 8bit-DIFF.dig as structural Verilog
module _8bit_DIFF (
  input  [7:0] A,
  input  [7:0] B,
  output [7:0] Diff,
  output Cout
);

  wire [7:0] not_1_out;

  assign not_1_out = ~B;  // Not not_1, 8 bits wide
  _8bit_AD _8bit_ad_1 (.A(A), .B(not_1_out), .Cin(1'b1), .S(Diff), .Cout(Cout));
endmodule
