// Digital circuit 8bit-LShift.dig as structural Verilog
module _8bit_LShift (
  input  [7:0] A,
  output [7:0] As
);

  LED led_1 (.in(A[7]));

  assign As = {A[6:0], 1'b0};

  // Notes on the sheet:
  //   A: Entrada de 8 bits para o valor.
endmodule
