// Digital circuit 2bit-COMP.dig as structural Verilog
module _2bit_COMP (
  input  [1:0] A,
  input  [1:0] B,
  output A_eq_B,
  output A_gt_B,
  output A_lt_B
);

  wire and_1_out, and_2_out, comp_1_p3, comp_1_p4, comp_1_p5, comp_2_p5, gt, lt;

  // COMP comp_1: pin names not known; wires that end beside it: A[0], B[0], comp_1_p3, comp_1_p4, comp_1_p5
  // COMP comp_2: pin names not known; wires that end beside it: A[1], B[1], gt, lt, comp_2_p5
  and and_1 (and_1_out, comp_1_p3, comp_2_p5);
  and and_2 (and_2_out, comp_1_p4, comp_2_p5);
  or or_1 (A_gt_B, and_1_out, lt);
  or or_2 (A_lt_B, and_2_out, gt);
  and and_3 (A_eq_B, comp_1_p5, comp_2_p5);
endmodule
