// Digital circuit AD.dig as structural Verilog
module AD (
  input  Cin,
  input  A,
  input  B,
  output Cout,
  output Sum
);

  wire hf_1_cout, hf_1_sum, hf_2_cout;

  HF hf_1 (.A(A), .B(B), .Sum(hf_1_sum), .Cout(hf_1_cout));
  HF hf_2 (.A(Cin), .B(hf_1_sum), .Sum(Sum), .Cout(hf_2_cout));
  or or_1 (Cout, hf_2_cout, hf_1_cout);
endmodule
