// Digital circuit CHOOSER.dig as structural Verilog
module CHOOSER (
  input  [7:0] A,
  input  Op,
  input  [7:0] B,
  output [7:0] AO,
  output [7:0] BO
);

  and and_1 (AO[0], Op, A[0]);
  and and_2 (AO[1], Op, A[1]);
  and and_3 (AO[2], Op, A[2]);
  and and_4 (AO[3], Op, A[3]);
  and and_5 (AO[4], Op, A[4]);
  and and_6 (AO[5], Op, A[5]);
  and and_7 (AO[6], Op, A[6]);
  and and_8 (AO[7], Op, A[7]);
  and and_9 (BO[0], Op, B[0]);
  and and_10 (BO[1], Op, B[1]);
  and and_11 (BO[2], Op, B[2]);
  and and_12 (BO[3], Op, B[3]);
  and and_13 (BO[4], Op, B[4]);
  and and_14 (BO[5], Op, B[5]);
  and and_15 (BO[6], Op, B[6]);
  and and_16 (BO[7], Op, B[7]);
endmodule
