// Digital circuit COMP.dig as structural Verilog
module COMP (
  input  A,
  input  B,
  input  _1_eq,
  output gt,
  output lt,
  output eq
);

  wire and_3_out, and_4_out, not_1_out, not_2_out;

  not not_1 (not_1_out, A);
  not not_2 (not_2_out, B);
  and and_1 (gt, A, _1_eq, not_2_out);
  and and_2 (lt, not_1_out, _1_eq, B);
  and and_3 (and_3_out, not_1_out, _1_eq, not_2_out);
  and and_4 (and_4_out, A, _1_eq, B);
  or or_1 (eq, and_3_out, and_4_out);
endmodule
