// Digital circuit Fetch Cycle.dig as structural Verilog
module Fetch_Cycle (
  input  Clock,
  input  in_2,
  output [7:0] Ac,
  output out_4,
  output out_5,
  output out_6,
  output Store,
  output Load,
  output Jump,
  output [3:0] Addr,
  output [3:0] out_11,
  output [7:0] out_12,
  output [7:0] out_13
);

  wire Clock_t, counter_1_ovf, decoder_1_out_0, Fetch, not_1_out, or_1_out, Ov, xor_1_out, xor_2_out;
  wire [1:0] demultiplexer_1_out_0;
  wire [2:0] demultiplexer_1_out_1;
  wire [2:2] demultiplexer_1_out_0_2;
  wire [3:0] counter_1_out, driver_1_out;

  assign {Addr, driver_1_out} = Clock_t ? out_13 : 8'bz;  // Driver driver_1
  Demultiplexer #(.Bits(3)) demultiplexer_1 (
    .sel(driver_1_out[0]), .in(driver_1_out[3:1]),
    .out_0({demultiplexer_1_out_0_2[2], demultiplexer_1_out_0}), .out_1(demultiplexer_1_out_1));
  Decoder #(.Selector_Bits(2)) decoder_1 (
    .sel(demultiplexer_1_out_0), .out_0(decoder_1_out_0), .out_1(Store), .out_2(Load), .out_3(Jump));
  // Probe on decoder_1_out_0
  // Probe on demultiplexer_1_out_0_2[2]
  // _8bit_ULA _8bit_ula_1: pin names not known; wires that end beside it: out_12, Ov, demultiplexer_1_out_1, out_4, out_13, out_5, Ac, out_6
  or or_1 (or_1_out, Jump, counter_1_ovf);
  xor xor_1 (xor_1_out, Clock_t, Store);
  Counter #(.Bits(4)) counter_1 (.en(1'b1), .C(Clock_t), .clr(or_1_out), .out(counter_1_out), .ovf(counter_1_ovf));
  Register #(.Bits(8)) u_Ac (.D(out_12), .C(Clock_t), .en(xor_1_out), .Q(Ac));
  assign Addr = Fetch ? counter_1_out : 4'bz;  // Driver driver_2
  BlockRAMDualPort #(.AddrBits(4), .isProgramMemory("true"), .Bits(8)) blockramdualport_1 (
    .A(Addr), .Din(out_12), .str(Load), .C(1'b1), .D(out_13));
  xor xor_2 (xor_2_out, Ov, in_2);
  and and_1 (Clock_t, xor_2_out, Clock);
  not not_1 (not_1_out, Clock_t);
  and and_2 (Fetch, xor_2_out, not_1_out);

  assign out_11 = Addr;

  // Other names for the same wires on the sheet: Data[7:0] = out_12; Execute = Clock_t; ORAM[7:0] = out_13;
  //   Str = Store; Wr = Load

  // Notes on the sheet:
  //   in_2: Instrução 1
endmodule
